# Fritzing sketch Super Máquina - Led (saved by Fritzing 0.9.3b)
circuit board: 8.46667cm x 5.64444cm
breadboards: 1

parts:
  R1 = Resistor [tolerance=±5% resistance=330 package=THT]
  LED1 = LED - 5mm [color="Red (633nm)" package="5 mm [THT]"]
  Componente1 = Arduino Uno (Rev3)

nets:
  N1: R1.Pin_0, Componente1.GND
  N2: R1.Pin_1, LED1.cathode
  N3: LED1.anode, Componente1.D13/SCK

// code stored in the sketch: Aula_2_-_Sequencial_de_LEDs.ino
/**
 * Sequencial de LEDs (efeito supermáquina)
 * @author - Daniel Casimiro Filho
 */

void setup() {
  pinMode(13, OUTPUT);
  }

void loop() {
  digitalWrite(13, HIGH);
  }
